# Fritzing sketch esp32s_bme280 (saved by Fritzing 0.9.3b)
perfboards: 1

parts:
  HLK-PM1 = HLK-PM01
  M1 = BME280
  ESP1 = ESP32-DevkitC
  J1 = screw terminal, 3 pins

nets:
  N1: HLK-PM1.AC#0, J1.pin3
  N2: HLK-PM1.AC#1, J1.pin1
  GND: HLK-PM1.-Vo, M1.GND, ESP1.GND
  N3: HLK-PM1.+Vo, ESP1.5V
  VIN: M1.VIN, ESP1.3V3
  N4: M1.SCL, ESP1.IO22
  N5: M1.SDA, ESP1.IO21

custom parts:
  BME280: Temperature Humidity Barometric presure Sensor
